# Fritzing sketch Задание - Влага (saved by Fritzing 1.0.1rc)
breadboards: 1

parts:
  DHT1 = Humidity and Temperature Sensor DHT11
  Part1 = Arduino Uno (Rev3)
  R1 = Resistor [tolerance=±5% power=0.25W resistance=4.7k package=THT]
  LED1 = RGB LED (com. cathode, rgb) [color="Red (633nm)" current=0.030A package="5 mm [THT]"]  # not connected

nets:
  VCC: DHT1.Vcc, Part1.5V, R1.Pin_1
  N1: DHT1.Data-signal, Part1.D9_PWM, R1.Pin_0
  N2: DHT1.GND_2, Part1.GND

custom parts:
  Humidity and Temperature Sensor DHT11: Digital relative humidity & temperature sensor DHT11
